# Fritzing sketch 8266_NodeMCU_with_reed (saved by Fritzing 0.9.4)
breadboards: 1

parts:
  NodeMCU_v1 = NodeMCU v3 LoLin [part_number=ESP8266]
  S1 = Reed switch [package=THT]
  R1 = Resistor [tolerance=±5% resistance=1k package="2010 [SMD]"]

nets:
  N1: NodeMCU_v1.D1, S1.pin_2, R1.Pin_0
  N2: NodeMCU_v1.3V3, S1.pin_1
  N3: NodeMCU_v1.GND, R1.Pin_1

custom parts:
  NodeMCU v3 LoLin: NodeMCU v3 LoLin NodeMCU (http://www.nodemcu.com/) is an open source IoT platform. It includes firmware (https://nodemcu-build.com/) which runs on the ESP8266 Wi-Fi SoC from Espressif Systems, and hardware which is based on the ESP-12E module. The term "NodeMCU" by default refers to the firmware rather than the dev kits. The firmware uses the Lua scripting language. It is based on the eLua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
