# Fritzing sketch Example Mockup sketch (saved by Fritzing 0.9.4)
breadboards: 1

parts:
  Bauteil1 = Arduino Uno (Rev3)
  S1 = Pushbutton [package="[THT]"]
  R1 = Resistor [tolerance=±5% resistance=10k package=THT]

nets:
  N1: Bauteil1.D2, S1.Pin_1, S1.Pin_2, R1.Pin_0
  N2: Bauteil1.5V, S1.Pin_3, S1.Pin_4
  N3: Bauteil1.GND, R1.Pin_1
