# Fritzing sketch sketch adurino with esp-01 wifi (saved by Fritzing 0.9.4)
breadboards: 1

parts:
  Bauteil1 = Arduino Uno (Rev3)
  U1 = ESP8266 WiFi Module [part_number=ESP8266]
  C1 = Electrolytic Capacitor [capacitance=10µF package="1010 [SMD, electrolytic]"]
  R1 = Resistor [tolerance=±5% resistance=1k package=THT]
  R2 = Resistor [tolerance=±5% resistance=2.2k package=THT]
  IC1 = V_REG_LD1117VXX [package=78xxl]

nets:
  N1: Bauteil1.D6_PWM, U1.TXD
  N2: Bauteil1.D7, R1.Pin_0
  N3: Bauteil1.5V, IC1.IN
  GND: Bauteil1.GND, U1.GND, C1.-, R2.Pin_1, IC1.GND
  N4: U1.RXD, R1.Pin_1, R2.Pin_0
  N5: U1.VCC, U1.CH_PD, C1.+, IC1.OUT

custom parts:
  ESP8266 WiFi Module: Generic WiFi Module based on the ESP8266 with onboard PCB antenna and UART communications
